# Fritzing sketch 8x8x8 LED Cube (saved by Fritzing 0.8.7b)
breadboards: 1

parts:
  Q1 = Basic FET P-Channel [package="TO220 [THT]"]
  Q2 = NPN-Transistor [package="TO92 [THT]"]
  R8 = 1K Ω Resistor [package=THT]
  R9 = 1K Ω Resistor [package=THT]
  U1 = 74HC595 [package="DIP16 [THT]"]
  R20 = 1K Ω Resistor [package=THT]
  LED11 = LED - 5mm [color="Red (633nm)" package="5 mm [THT]"]
  R21 = 1K Ω Resistor [package=THT]
  R22 = 1K Ω Resistor [package=THT]
  R23 = 1K Ω Resistor [package=THT]
  R24 = 1K Ω Resistor [package=THT]
  R25 = 1K Ω Resistor [package=THT]
  R26 = 1K Ω Resistor [package=THT]
  R27 = 1K Ω Resistor [package=THT]
  LED12 = LED - 5mm [color="Red (633nm)" package="5 mm [THT]"]
  LED13 = LED - 5mm [color="Red (633nm)" package="5 mm [THT]"]
  LED14 = LED - 5mm [color="Red (633nm)" package="5 mm [THT]"]
  LED15 = LED - 5mm [color="Red (633nm)" package="5 mm [THT]"]
  LED16 = LED - 5mm [color="Red (633nm)" package="5 mm [THT]"]
  LED17 = LED - 5mm [color="Red (633nm)" package="5 mm [THT]"]
  LED18 = LED - 5mm [color="Red (633nm)" package="5 mm [THT]"]
  U2 = 74HC595 [package="DIP16 [THT]"]
  LED19 = LED - 5mm [color="Red (633nm)" package="5 mm [THT]"]
  LED20 = LED - 5mm [color="Red (633nm)" package="5 mm [THT]"]
  LED21 = LED - 5mm [color="Red (633nm)" package="5 mm [THT]"]
  LED22 = LED - 5mm [color="Red (633nm)" package="5 mm [THT]"]
  LED23 = LED - 5mm [color="Red (633nm)" package="5 mm [THT]"]
  LED24 = LED - 5mm [color="Red (633nm)" package="5 mm [THT]"]
  LED25 = LED - 5mm [color="Red (633nm)" package="5 mm [THT]"]
  LED26 = LED - 5mm [color="Red (633nm)" package="5 mm [THT]"]
  R28 = 1K Ω Resistor [package=THT]
  R29 = 1K Ω Resistor [package=THT]
  R30 = 1K Ω Resistor [package=THT]
  R31 = 1K Ω Resistor [package=THT]
  R32 = 1K Ω Resistor [package=THT]
  R33 = 1K Ω Resistor [package=THT]
  R34 = 1K Ω Resistor [package=THT]
  R35 = 1K Ω Resistor [package=THT]

nets:
  N1: Q1.gate, Q2.C, R9.Pin_1
  5V: Q1.drain, R9.Pin_0, U1.MR, U1.VCC, U2.MR, U2.VCC
  N2: Q1.source, LED11.anode, LED12.anode, LED13.anode, LED14.anode, LED15.anode, LED16.anode, LED17.anode, LED18.anode, LED24.anode
  GND: Q2.E, U1.GND, U1.OE, U2.GND, U2.OE
  N3: Q2.B, R8.Pin_1
  net label: R8.Pin_0, U1.SH_CP, U1.ST_CP, U1.DS, U2.SH_CP, U2.ST_CP
  N4: U1.Q1, R26.Pin_1
  N5: U1.Q2, R25.Pin_1
  N6: U1.Q3, R24.Pin_1
  N7: U1.Q4, R23.Pin_1
  N8: U1.Q5, R22.Pin_1
  N9: U1.Q6, R21.Pin_1
  N10: U1.Q7, R20.Pin_1
  N11: U1.Q7', U2.DS
  N12: U1.Q0, R27.Pin_1
  N13: R20.Pin_0, LED11.cathode
  N14: R21.Pin_0, LED12.cathode
  N15: R22.Pin_0, LED13.cathode
  N16: R23.Pin_0, LED14.cathode
  N17: R24.Pin_0, LED15.cathode
  N18: R25.Pin_0, LED16.cathode
  N19: R26.Pin_0, LED17.cathode
  N20: R27.Pin_0, LED18.cathode
  N21: U2.Q1, R29.Pin_1
  N22: U2.Q2, R30.Pin_1
  N23: U2.Q3, R31.Pin_1
  N24: U2.Q4, R32.Pin_1
  N25: U2.Q5, R33.Pin_1
  N26: U2.Q6, R34.Pin_1
  N27: U2.Q7, R35.Pin_1
  N28: U2.Q0, R28.Pin_1
  N29: LED19.cathode, R28.Pin_0
  N30: LED19.anode, LED20.anode, LED21.anode, LED22.anode
  N31: LED20.cathode, R29.Pin_0
  N32: LED21.cathode, R30.Pin_0
  N33: LED22.cathode, R31.Pin_0
  N34: LED23.cathode, R32.Pin_0
  N35: LED23.anode, LED25.anode, LED26.anode
  N36: LED24.cathode, R33.Pin_0
  N37: LED25.cathode, R34.Pin_0
  N38: LED26.cathode, R35.Pin_0

notes:
  Eight shift registers independently control the "ground" for each of the 64 LED pillars. Note how pin 10 from previous shift register is used as input (14) for the next shift register. Arduino shifts all 64 bits for the layer and then supplies (+) on the desired layers via one of the 8 MOSFETs.
  One of the 8 MOSFETs supply power to one of the 8x8 layer grids once the desired pattern for that layer has been setup in the shift registers.

custom parts:
  1K Ω Resistor: A generic resistor (0.25W)
