# Fritzing sketch LearnShiftOut (saved by Fritzing 0.8.7b)
breadboards: 1

parts:
  Part1 = Arduino Uno (Rev3)
  U1 = 74HC595 [package="DIP16 [THT]"]
  U2 = 74HC595 [package="DIP16 [THT]"]

nets:
  N1: Part1.D11_PWM/MOSI, U1.ST_CP, U2.ST_CP
  N2: Part1.D12/MISO, U1.SH_CP, U2.SH_CP
  N3: Part1.D13/SCK, U1.DS
  N4: U1.Q7', U2.DS
  VCC: U1.MR, U1.VCC, U2.MR, U2.VCC
  N5: U1.OE, U2.OE
