# Fritzing sketch pong2 (saved by Fritzing 0.9.2b)
breadboards: 1

parts:
  Part1 = Arduino Uno (Rev3)
  LED1 = LEDs [package=led10mm]
  LED2 = LEDs [package=led10mm]
  LED3 = LEDs [package=led10mm]
  LED4 = LEDs [package=led10mm]
  LED5 = LEDs [package=led10mm]
  LED6 = LEDs [package=led10mm]
  LED7 = LEDs [package=led10mm]
  LED8 = LEDs [package=led10mm]
  R1 = Resistor [tolerance=±5% resistance=220 package=THT]
  R2 = Resistor [tolerance=±5% resistance=220 package=THT]
  R3 = Resistor [tolerance=±5% resistance=220 package=THT]
  R4 = Resistor [tolerance=±5% resistance=220 package=THT]
  R5 = Resistor [tolerance=±5% resistance=220 package=THT]
  R6 = Resistor [tolerance=±5% resistance=220 package=THT]
  R7 = Resistor [tolerance=±5% resistance=220 package=THT]
  R8 = Resistor [tolerance=±5% resistance=220 package=THT]
  S1 = Pushbutton [package="[THT]"]
  S2 = Pushbutton [package="[THT]"]

nets (from the breadboard view):
  N1: Part1.D8, R4.Pin_0
  N2: Part1.D9_PWM, R3.Pin_0
  N3: Part1.D10_PWM/SS, R2.Pin_0
  N4: Part1.D11_PWM/MOSI, R1.Pin_0
  N5: Part1.GND, LED1.A, LED2.A, LED3.A, LED5.A, LED6.A, LED7.A, LED8.A, S1.Pin_1, S1.Pin_2, S2.Pin_3, S2.Pin_4
  N6: Part1.D2, S1.Pin_3, S1.Pin_4
  N7: Part1.D4, R8.Pin_0
  N8: Part1.D5_PWM, R7.Pin_0
  N9: Part1.D6_PWM, R6.Pin_0
  N10: Part1.D7, R5.Pin_0
  N11: LED1.C, R1.Pin_1
  N12: LED2.C, R2.Pin_1
  N13: LED3.C, R3.Pin_1
  N14: LED4.C, R4.Pin_1
  N15: LED5.C, R5.Pin_1
  N16: LED6.C, R6.Pin_1
  N17: LED7.C, R7.Pin_1
  N18: LED8.C, R8.Pin_1
  N19: S2.Pin_1, S2.Pin_2
