# Fritzing sketch Wiring_ESP8266_with_FTDI (saved by Fritzing 0.8.7b)
breadboards: 1

parts:
  U1 = Voltage Regulator - 3.3V [package="TO220 [THT]"]
  Espessif_Serial_Wifi_Modul_1 = ESP8266 ESP01 [part_number=ESP8266 package=THT]
  LED1 = LED - 5mm [color="Red (633nm)" package="5 mm [THT]"]
  R1 = Resistor [tolerance=±5% resistance=1k package=THT]
  Part1 = FTDI Basic Programmer
  JACK1 = 2.1mm Barrel Jack with Terminal Block
  R2 = Resistor [tolerance=±5% resistance=1k package=THT]
  R3 = Resistor [tolerance=±5% resistance=1k package=THT]
  S2 = Momentary Switch [package=tactile-pth]
  R4 = Resistor [tolerance=±5% resistance=1.8k package=THT]

nets:
  N1: U1.input_voltage, JACK1.POS
  GND: U1.GND, Espessif_Serial_Wifi_Modul_1.GND, Part1.GND, JACK1.NEG, S2.2, R4.Pin_0
  N2: U1.output_voltage, Espessif_Serial_Wifi_Modul_1.VCC, Espessif_Serial_Wifi_Modul_1.GPIO16, Espessif_Serial_Wifi_Modul_1.CH_PD, R1.Pin_1, R2.Pin_0
  N3: Espessif_Serial_Wifi_Modul_1.RXD, R3.Pin_0, R4.Pin_1
  N4: Espessif_Serial_Wifi_Modul_1.TXD, Part1.RXI
  N5: Espessif_Serial_Wifi_Modul_1.GPIO00, R2.Pin_1, S2.3
  N6: Espessif_Serial_Wifi_Modul_1.GPIO02, LED1.cathode
  N7: LED1.anode, R1.Pin_0
  N8: Part1.TXO, R3.Pin_1

custom parts:
  ESP8266 ESP01: Generic WiFi Module based on the ESP8266 with onboard PCB antenna and UART communications
